# Fritzing sketch SFBD_Gateway (saved by Fritzing 0.9.10b)
circuit board: 8.15997cm x 8.66474cm
breadboards: 1

parts:
  Mod2 = ossoyoo-lora-module
  J3 = male pin header, 3 pins [form="♂ (male)"]
  C4 = Capacitor [package=cap-pth-small2]
  R3 = Resistor [tolerance=±5% resistance=410 power=0.25 package=THT]
  R4 = Resistor [tolerance=±5% resistance=10k power=0.25 package=THT]
  J4 = Power Jack [package=power_jack_pth_lock]
  R5 = Resistor [tolerance=±5% resistance=410 power=0.25 package=THT]
  R6 = Resistor [tolerance=±5% resistance=410 power=0.25 package=THT]
  S2 = Momentary Switch 6mm 2pin
  C5 = Electrolytic Capacitor [capacitance=100µF voltage=35V package="200 mil [THT, electrolytic]"]
  C6 = Electrolytic Capacitor [capacitance=100µF voltage=35V package="200 mil [THT, electrolytic]"]
  Mod1 = TTGO-T-Call-V1.3-ESP32 [package=THT]

nets:
  M0: Mod2.M0, Mod1.14
  M1: Mod2.M1, Mod1.12
  M_TX > L_RX: Mod2.RXD, R5.Pin_0, Mod1.19
  M_RX > L_TX: Mod2.TXD, R6.Pin_0, Mod1.18
  5V: Mod2.VCC, J4.PWR, R5.Pin_1, R6.Pin_1, C5.+, C6.+, Mod1.5V
  GND: Mod2.GND, C4.2, J4.GND, S2.1, C5.-, C6.-, Mod1.GND
  N1: J3.pin1, J3.pin2, J3.pin3
  N2: C4.1, R3.Pin_0, R4.Pin_1, S2.2
  button: R3.Pin_1, Mod1.0
  3.3V: R4.Pin_0, Mod1.3V3

notes:
  Smart Fish BD, 0.1

custom parts:
  ossoyoo-lora-module: Osoyoo Long Distance wireless transceiver Uart LoRa Module.
  Momentary Switch 6mm 2pin: Momentary Switch 6mm 2 pin Button commonly used for reset or general input.
  TTGO-T-Call-V1.3-ESP32: LILYGO® TTGO T-Call V1.3 ESP32 Wireless Module GPRS Antenna SIM Card SIM800L Module
