# Fritzing sketch SFBD_Sensor (saved by Fritzing 0.9.10b)
circuit board: 5.41cm x 6.27997cm
breadboards: 1

parts:
  S1 = PH meter [package=THT]
  J1 = female pin header, 3 pins [form="♀ (female)"]
  J2 = female pin header, 3 pins [form="♀ (female)"]
  J3 = female pin header, 3 pins [form="♀ (female)"]
  M1 = STM32F103C8T6 blue mini board
  J4 = female pin header, 4 pins [form="♀ (female)"]
  J8 = female pin header, 3 pins [form="♀ (female)"]
  J9 = female pin header, 3 pins [form="♀ (female)"]
  J10 = female pin header, 3 pins [form="♀ (female)"]
  J11 = female pin header, 3 pins [form="♀ (female)"]
  J12 = female pin header, 2 pins [form="♀ (female)"]
  J13 = female pin header, 2 pins [form="♀ (female)"]
  J14 = female pin header, 2 pins [form="♀ (female)"]
  J15 = female pin header, 3 pins [form="♀ (female)"]
  J16 = Power Jack [package=power_jack_slot]
  C8 = Electrolytic Capacitor [capacitance=100µF voltage=35V package="200 mil [THT, electrolytic]"]
  C9 = Electrolytic Capacitor [capacitance=100µF voltage=35V package="200 mil [THT, electrolytic]"]
  J18 = female pin header, 7 pins [form="♀ (female)"]
  R9 = Resistor [tolerance=±5% resistance=410 power=0.25 package=THT]
  R10 = Resistor [tolerance=±5% resistance=410 power=0.25 package=THT]

nets:
  pH: S1.pin1, M1.A1
  3.3V: S1.pin2, J1.pin2, J2.pin2, J3.pin2, M1.3.3V, M1.3.3, J8.pin2, J15.pin2
  GND: S1.pin3, J1.pin1, J2.pin1, J3.pin1, M1.G, M1.GND, J4.pin4, J8.pin1, J9.pin1, J10.pin1, J11.pin1, J12.pin2, J13.pin2, J14.pin2, J15.pin3, J16.GNDBREAK, J16.GND, C8.-, C9.-, J18.pin1, J18.pin2, J18.pin7
  Dissolved O2: J1.pin3, M1.A0
  TDS: J2.pin3, M1.A4
  Temp: J3.pin3, M1.A5
  STM32 TX > TTL RX: M1.A8, J4.pin2
  ttl tx: M1.A9, J4.pin3
  5V: M1.5V, J4.pin1, J9.pin2, J10.pin2, J11.pin2, J12.pin1, J13.pin1, J14.pin1, J15.pin1, J16.PWR, C8.+, C9.+, J18.pin6, R9.Pin_1, R10.Pin_1
  M_TX > L_RX: M1.A2, J18.pin3, R9.Pin_0
  M_RX > L_TX: M1.A3, J18.pin4, R10.Pin_0
  rain: M1.B0, J8.pin3
  Food Full: M1.B1, J11.pin3
  Food Medium: M1.B10, J10.pin3
  Food Empty: M1.B11, J9.pin3
