# Fritzing sketch SFBD_Switch (saved by Fritzing 0.9.10b)
circuit board: 7.39803cm x 8.09408cm
breadboards: 1

parts:
  M1 = STM32F103C8T6 blue mini board
  C7 = Electrolytic Capacitor [capacitance=100µF voltage=35V package="200 mil [THT, electrolytic]"]
  C8 = Electrolytic Capacitor [capacitance=100µF voltage=35V package="200 mil [THT, electrolytic]"]
  MOD1 = ossoyoo-lora-module
  J6 = male pin header, 3 pins [form="♂ (male)"]
  J8 = male pin header, 6 pins [form="♂ (male)"]
  R7 = Resistor [tolerance=±5% resistance=410 power=0.25 package=THT]
  R8 = Resistor [tolerance=±5% resistance=410 power=0.25 package=THT]
  J9 = male pin header, 10 pins [form="♂ (male)"]
  J5 = Power Jack [package=power_jack_slot]
  Rx_TX_G_3_3 = female pin header, 4 pins [form="♀ (female)"]

nets:
  Relay 1 (in8): M1.B12, J9.pin9
  Relay 2 (in7): M1.B13, J9.pin8
  Relay 3 (in6): M1.B14, J9.pin7
  Relay 4 (in5): M1.B15, J9.pin6
  Relay 13: M1.A8
  N1: M1.A9, Rx_TX_G_3_3.pin1
  N2: M1.A10, Rx_TX_G_3_3.pin2
  Relay 14: M1.A11
  Relay 15: M1.A12
  Relay 5 (in4): M1.A15, J9.pin5
  Relay 6 (in3): M1.B3, J9.pin4
  Relay 7 (in2): M1.B4, J9.pin3
  Relay 8 (in1): M1.B5, J9.pin2
  Relay 9 (in4): M1.B6, J8.pin5
  Relay 10 (in3): M1.B7, J8.pin4
  Relay 11 (in2): M1.B8, J8.pin3
  Relay 12 (in1): M1.B9, J8.pin2
  5V: M1.5V, C7.+, C8.+, MOD1.VCC, J8.pin6, R7.Pin_1, R8.Pin_1, J9.pin10, J5.PWR
  GND: M1.G, M1.GND, C7.-, C8.-, MOD1.GND, J8.pin1, J9.pin1, J5.GNDBREAK, Rx_TX_G_3_3.pin3
  M0: M1.A0, MOD1.M0
  M1: M1.A1, MOD1.M1
  M_TX > L_RX: M1.A2, MOD1.RXD, R7.Pin_0
  M_RX > L_TX: M1.A3, MOD1.TXD, R8.Pin_0
  Relay 16: M1.B1
  N3: M1.3.3V, Rx_TX_G_3_3.pin4
  N4: J6.pin1, J6.pin2, J6.pin3

notes:
  Smart Fish BD, 0.1

custom parts:
  ossoyoo-lora-module: Osoyoo Long Distance wireless transceiver Uart LoRa Module.
